// Logisim project midway.circ as structural Verilog: 4 circuits, main circuit Nomad
module Nomad (
  input  Pwr
);

  wire and_1_out, and_3_out, and_4_out, and_5_out, AOut, Cl, demultiplexer_1_out1, demultiplexer_1_out2,
       demultiplexer_1_out3, demultiplexer_1_out4, demultiplexer_1_out5, demultiplexer_2_out0,
       demultiplexer_2_out1, demultiplexer_2_out2, demultiplexer_2_out3, demultiplexer_3_out0,
       demultiplexer_3_out1, demultiplexer_3_out2, demultiplexer_3_out3, demultiplexer_3_out4,
       demultiplexer_3_out5, demultiplexer_3_out6, demultiplexer_3_out7, demultiplexer_3_out10,
       demultiplexer_3_out11, demultiplexer_3_out12, demultiplexer_3_out13, Jmp, not_1_out, or_1_out, RamS,
       ROut;
  wire [1:0] Fl;
  wire [3:0] Op;
  wire [7:0] _0i, _0ii, _0s, _0x, _1i, _1ii, _1s, _1x, _2s, _2x, _3s, _3x, A, A_q, AO, B, B_q, counter_1_q,
       J, M, multiplexer_3_out, O, Or, RAM, RS;
  wire [15:14] rom_1_data;

  Counter counter_1 (.load(Jmp), .D(J), .count(Cl), .Q(counter_1_q), .clk(Cl), .clr(Pwr));  // open: carry
  Clock u_Cl (.out(Cl));
  Demultiplexer #(.select(3), .enable("false")) demultiplexer_1 (
    .out1(demultiplexer_1_out1), .out2(demultiplexer_1_out2), .out3(demultiplexer_1_out3),
    .out4(demultiplexer_1_out4), .out5(demultiplexer_1_out5), .in(1'b1), .sel(Op[2:0]));  // open: out0, out6, out7
  Demultiplexer #(.select(2), .enable("false")) demultiplexer_2 (
    .out0(demultiplexer_2_out0), .out1(demultiplexer_2_out1), .out2(demultiplexer_2_out2),
    .out3(demultiplexer_2_out3), .in(1'b1), .sel(Fl));
  Multiplexer #(.select(4), .width(8), .enable("false")) multiplexer_1 (
    .in0(_0x), .in1(_1x), .in2(_2x), .in3(_3x), .in4(_0s), .in5(_1s), .in6(_2s), .in7(_3s), .in8(_0i),
    .in9(_1i), .in10(A), .in11(B), .in12(M), .in13(J), .out(RS), .sel(Or[3:0]));  // open: in14, in15
  Demultiplexer #(.select(4), .enable("false")) demultiplexer_3 (
    .out0(demultiplexer_3_out0), .out1(demultiplexer_3_out1), .out2(demultiplexer_3_out2),
    .out3(demultiplexer_3_out3), .out4(demultiplexer_3_out4), .out5(demultiplexer_3_out5),
    .out6(demultiplexer_3_out6), .out7(demultiplexer_3_out7), .out10(demultiplexer_3_out10),
    .out11(demultiplexer_3_out11), .out12(demultiplexer_3_out12), .out13(demultiplexer_3_out13), .in(ROut),
    .sel(M[3:0]));  // open: out8, out9, out14, out15
  not not_1 (not_1_out, demultiplexer_2_out3);
  ROM #(.dataWidth(16)) rom_1 (.addr(counter_1_q), .data({rom_1_data, Or, Fl, Op}), .sel(1'b1));
  and and_1 (and_1_out, demultiplexer_1_out3, demultiplexer_2_out0);
  and and_2 (RamS, demultiplexer_2_out2, demultiplexer_1_out5);
  and and_3 (and_3_out, demultiplexer_1_out3, demultiplexer_2_out1);
  and and_4 (and_4_out, demultiplexer_1_out4, demultiplexer_2_out1, not_1_out);
  Register u__0x (.D(O), .en(demultiplexer_3_out0), .Q(_0x), .clk(Cl), .clr(Pwr));
  Register u__0s (.D(O), .en(demultiplexer_3_out7), .Q(_0s), .clk(Cl), .clr(Pwr));
  Register u__0i (.D(_0ii), .en(1'b1), .Q(_0i), .clk(Cl), .clr(Pwr));
  Register u_M (.D(O), .en(demultiplexer_3_out12), .Q(M), .clk(Cl), .clr(Pwr));
  or or_1 (or_1_out, demultiplexer_2_out0, demultiplexer_2_out2);
  or or_2 (AOut, and_1_out, and_4_out);
  Register u__1x (.D(O), .en(demultiplexer_3_out1), .Q(_1x), .clk(Cl), .clr(Pwr));
  Register u__1s (.D(O), .en(demultiplexer_3_out6), .Q(_1s), .clk(Cl), .clr(Pwr));
  Register u__1i (.D(_1ii), .en(1'b1), .Q(_1i), .clk(Cl), .clr(Pwr));
  Register u_J (.D(O), .en(demultiplexer_3_out13), .Q(J), .clk(Cl), .clr(Pwr));
  or or_3 (ROut, demultiplexer_1_out1, and_3_out, and_5_out, demultiplexer_1_out2);
  and and_5 (and_5_out, demultiplexer_1_out4, or_1_out);
  Register u__2x (.D(O), .en(demultiplexer_3_out2), .Q(_2x), .clk(Cl), .clr(Pwr));
  Register u__2s (.D(O), .en(demultiplexer_3_out5), .Q(_2s), .clk(Cl));  // open: clr
  Register u_A (.D(O), .en(demultiplexer_3_out10), .Q(A_q), .clk(Cl), .clr(Pwr));
  Register u__3x (.D(O), .en(demultiplexer_3_out3), .Q(_3x), .clk(Cl), .clr(Pwr));
  Register u__3s (.D(O), .en(demultiplexer_3_out4), .Q(_3s), .clk(Cl), .clr(Pwr));
  Register u_B (.D(O), .en(demultiplexer_3_out11), .Q(B_q), .clk(Cl), .clr(Pwr));
  Multiplexer #(.select(5), .width(8), .enable("false")) multiplexer_2 (
    .in4(AO), .in5(AO), .in6(AO), .in7(AO), .in8(AO), .in9(AO), .in10(AO), .in11(AO), .in16(Or), .in17(Or),
    .in18(Or), .in19(Or), .in20(RS), .in21(RS), .in22(RAM), .out(O), .sel({Fl, Op[2:0]}));  // open: in0, in1, in2, in3, in12, in13, in14, in15, in23, in24, in25, in26, in27, in28, in29, in30, in31
  Multiplexer #(.width(8), .enable("false")) multiplexer_3 (.in0(M), .in1(Or), .out(multiplexer_3_out), .sel(RamS));
  ALU alu_1 (.A(A_q), .B(B_q), .Operation(Op), .Flag(Fl), .Out(AO), .J(Jmp));
  RAM #(.bus("separate")) ram_1 (
    .addr(multiplexer_3_out), .din(O), .data(RAM), .str(AOut), .sel(1'b1), .clk(Cl), .ld(Cl), .clr(Pwr));
  _7_Segment_Display u_7_segment_display_1 (
    .g(_2s[0]), .f(_2s[1]), .a(_2s[2]), .b(_2s[3]), .e(_2s[4]), .d(_2s[5]), .c(_2s[6]), .dp(_2s[7]));
  Button button_1 (.out(_1ii[7]));
  Button button_2 (.out(_1ii[4]));
  Button button_3 (.out(_1ii[6]));
  Button button_4 (.out(_1ii[5]));
  _7_Segment_Display u_7_segment_display_2 (
    .g(_3s[0]), .f(_3s[1]), .a(_3s[2]), .b(_3s[3]), .e(_3s[4]), .d(_3s[5]), .c(_3s[6]), .dp(_3s[7]));
  TTY tty_1 (.data(_1s[6:0]), .clk(Cl), .we(Cl), .clr(_1s[7]));
  Button button_5 (.out(_1ii[1]));
  Button button_6 (.out(_1ii[3]));
  Button button_7 (.out(_1ii[0]));
  Button button_8 (.out(_1ii[2]));
  Keyboard keyboard_1 (.re(Cl), .avail(_0ii[7]), .data(_0ii[6:0]));  // open: clk, clr
  LED led_1 (.in(_0s[6]));
  LED led_2 (.in(_0s[5]));
  LED led_3 (.in(_0s[7]));
  LED led_4 (.in(_0s[3]));
  LED led_5 (.in(_0s[1]));
  LED led_6 (.in(_0s[4]));
  LED led_7 (.in(_0s[2]));
  LED led_8 (.in(_0s[0]));

  // Notes on the sheet:
  //   Register Select Based off Operand (MOS)
  //   MOV to Address
  //   Write Operation Enable
  //   MOV to Reg
  //   MOS to Address
  //   Reg Type / Num
  //   MOS to Reg
  //   Inputs tunnels have double ii to represent actual input device
  //   Memory
  //   Output Manager
  //   Buttons
  //   Screen
  //   Keyboard
endmodule

module full_adder (
  input  A,
  input  B,
  input  Cin,
  output Cout,
  output S
);

  wire and_1_out, and_2_out, xor_1_out;

  and and_1 (and_1_out, B, Cin);
  and and_2 (and_2_out, A, xor_1_out);
  xor xor_1 (xor_1_out, B, Cin);
  xor xor_2 (S, A, xor_1_out);
  or or_1 (Cout, and_2_out, and_1_out);
endmodule

module _8_Bit_Adder (
  input  [7:0] A,
  input  [7:0] B,
  input  Cin,
  output [7:0] out_4,
  output Cout
);

  wire full_adder_1_cout, full_adder_2_cout, full_adder_3_cout, full_adder_4_cout, full_adder_5_cout,
       full_adder_6_cout, full_adder_7_cout;

  full_adder full_adder_1 (.A(A[0]), .B(B[0]), .Cin(Cin), .Cout(full_adder_1_cout), .S(out_4[0]));
  full_adder full_adder_2 (.A(A[1]), .B(B[1]), .Cin(full_adder_1_cout), .Cout(full_adder_2_cout), .S(out_4[1]));
  full_adder full_adder_3 (.A(A[2]), .B(B[2]), .Cin(full_adder_2_cout), .Cout(full_adder_3_cout), .S(out_4[2]));
  full_adder full_adder_4 (.A(A[3]), .B(B[3]), .Cin(full_adder_3_cout), .Cout(full_adder_4_cout), .S(out_4[3]));
  full_adder full_adder_5 (.A(A[4]), .B(B[4]), .Cin(full_adder_4_cout), .Cout(full_adder_5_cout), .S(out_4[4]));
  full_adder full_adder_6 (.A(A[5]), .B(B[5]), .Cin(full_adder_5_cout), .Cout(full_adder_6_cout), .S(out_4[5]));
  full_adder full_adder_7 (.A(A[6]), .B(B[6]), .Cin(full_adder_6_cout), .Cout(full_adder_7_cout), .S(out_4[6]));
  full_adder full_adder_8 (.A(A[7]), .B(B[7]), .Cin(full_adder_7_cout), .Cout(Cout), .S(out_4[7]));
endmodule

module ALU (
  input  [7:0] A,
  input  [7:0] B,
  input  [3:0] Operation,
  input  [1:0] Flag,
  output [7:0] Out,
  output J
);

  wire comparator_1_eq, comparator_2_eq, comparator_2_gt, comparator_2_lt, comparator_3_eq, comparator_4_eq,
       comparator_5_gt, multiplexer_3_out, not_3_out;
  wire [7:0] and_1_out, divider_1_out, multiplexer_1_out, multiplexer_2_out, multiplier_1_out,
       n8_bit_adder_1_out_4, n8_bit_adder_2_out_4, not_1_out, not_2_out, or_1_out, xor_1_out;

  Comparator #(.width(4)) comparator_1 (.a(Operation), .b(4'b0010), .eq(comparator_1_eq));  // open: gt, lt
  _8_Bit_Adder u_8_bit_adder_1 (.A(A), .B(B), .Cin(1'b0), .out_4(n8_bit_adder_1_out_4));  // open: Cout
  _8_Bit_Adder u_8_bit_adder_2 (.A(A), .B(not_1_out), .Cin(1'b1), .out_4(n8_bit_adder_2_out_4));  // open: Cout
  assign not_1_out = ~B;  // NOT_Gate not_1, 8 bits wide
  Multiplier multiplier_1 (.a(A), .b(B), .out(multiplier_1_out));  // open: cin, cout
  Divider divider_1 (.a(A), .b(B), .out(divider_1_out));  // open: upper, rem
  assign and_1_out = A & B;  // AND_Gate and_1, 8 bits wide
  assign not_2_out = ~A;  // NOT_Gate not_2, 8 bits wide
  assign or_1_out = A | B;  // OR_Gate or_1, 8 bits wide
  assign xor_1_out = A ^ B;  // XOR_Gate xor_1, 8 bits wide
  Comparator #(.mode("unsigned")) comparator_2 (
    .a(A), .b(B), .gt(comparator_2_gt), .eq(comparator_2_eq), .lt(comparator_2_lt));
  Comparator #(.width(4)) comparator_3 (.a(Operation), .b(4'b0111), .eq(comparator_3_eq));  // open: gt, lt
  Comparator #(.width(4)) comparator_4 (.a(Operation), .b(4'b0001), .eq(comparator_4_eq));  // open: gt, lt
  not not_3 (not_3_out, comparator_2_eq);
  Multiplexer #(.select(2), .width(8)) multiplexer_1 (
    .in0(n8_bit_adder_1_out_4), .in1(n8_bit_adder_2_out_4), .in2(multiplier_1_out), .in3(divider_1_out),
    .out(multiplexer_1_out), .sel(Flag), .en(comparator_4_eq));
  Multiplexer #(.select(2), .width(8)) multiplexer_2 (
    .in0(and_1_out), .in1(not_2_out), .in2(or_1_out), .in3(xor_1_out), .out(multiplexer_2_out), .sel(Flag),
    .en(comparator_1_eq));
  Multiplexer #(.select(2), .disabled(0)) multiplexer_3 (
    .in0(comparator_2_gt), .in1(comparator_2_eq), .in2(not_3_out), .in3(comparator_2_lt),
    .out(multiplexer_3_out), .sel(Flag), .en(comparator_3_eq));
  Comparator #(.width(4)) comparator_5 (.a(Operation), .b(4'b0110), .gt(comparator_5_gt));  // open: eq, lt
  Multiplexer #(.select(2), .width(8), .enable("false")) multiplexer_4 (
    .in1(multiplexer_1_out), .in2(multiplexer_2_out), .out(Out), .sel(Operation[1:0]));  // open: in0, in3
  or or_2 (J, multiplexer_3_out, comparator_5_gt);

  // Notes on the sheet:
  //   Add/Sub
  //   GR/EQ/NE/LT
  //   Why so many comparators? Well, the reason is simple. In a real circuit you'd probably use AND gates with all of the split inputs. 
  //   In practice, that takes forever, and is ugly. Comparators simulate faster, and take up less screen space. Achieving the same effect, they do what I need.
  //   ADD/SUB/MUL/DIV
  //   AND/NOT/OR/XOR
endmodule
