// Logisim project nomad.circ as structural Verilog: 4 circuits, main circuit main
module main (
  input  Clear
);

  wire Cl, clock_1_out, demultiplexer_1_out0, demultiplexer_1_out1, demultiplexer_1_out2,
       demultiplexer_1_out3, demultiplexer_1_out4, demultiplexer_1_out5, demultiplexer_1_out6,
       demultiplexer_1_out7, demultiplexer_1_out8, demultiplexer_1_out9, demultiplexer_1_out10,
       demultiplexer_1_out11, demultiplexer_2_out1, demultiplexer_2_out2, demultiplexer_2_out3,
       demultiplexer_2_out4, demultiplexer_2_out5, demultiplexer_2_out6, demultiplexer_2_out7,
       demultiplexer_2_out8, demultiplexer_2_out9, demultiplexer_2_out10, J, n7_segment_display_1_p1,
       n7_segment_display_2_p1, n7_segment_display_3_p1, RegEnable, WriteAdr;
  wire [3:0] button_3_out, button_7_out, joystick_1_x, joystick_1_y, Operation, rs;
  wire [7:0] A, ALUOut, B, counter_1_q, Dip, i0, i1, i2, i3, KB, O, Operand, RAMOut, RegisterRead, s0, s1,
       s2, x0, x1, x2, x3, x4, x5, x6;

  Counter counter_1 (
    .clr(Clear), .load(J), .up(clock_1_out), .count(clock_1_out), .clk(clock_1_out), .D(Operand),
    .Q(counter_1_q));  // open: carry
  Clock clock_1 (.out(clock_1_out));
  Clock clock_2 (.out(Cl));
  Demultiplexer #(.select(4), .enable("false")) demultiplexer_1 (
    .out0(demultiplexer_1_out0), .out1(demultiplexer_1_out1), .out2(demultiplexer_1_out2),
    .out3(demultiplexer_1_out3), .out4(demultiplexer_1_out4), .out5(demultiplexer_1_out5),
    .out6(demultiplexer_1_out6), .out7(demultiplexer_1_out7), .out8(demultiplexer_1_out8),
    .out9(demultiplexer_1_out9), .out10(demultiplexer_1_out10), .out11(demultiplexer_1_out11),
    .in(RegEnable), .sel(rs));  // open: out12, out13, out14, out15
  Register u_A (.D(O), .en(demultiplexer_1_out0), .clk(Cl), .Q(A), .clr(Clear));
  Register u_x2 (.D(O), .en(demultiplexer_1_out4), .clk(Cl), .Q(x2), .clr(Clear));
  Register u_x6 (.D(O), .en(demultiplexer_1_out8), .clk(Cl), .Q(x6), .clr(Clear));
  Register u_i0 (.D(KB), .en(Cl), .clk(Cl), .Q(i0), .clr(Clear));
  ROM #(.dataWidth(16)) rom_1 (.addr(counter_1_q), .data({Operation, rs, Operand}));
  Register u_B (.D(O), .en(demultiplexer_1_out1), .clk(Cl), .Q(B), .clr(Clear));
  Register u_x3 (.D(O), .en(demultiplexer_1_out5), .clk(Cl), .Q(x3), .clr(Clear));
  Register u_s0 (.D(O), .en(demultiplexer_1_out9), .clk(Cl), .Q(s0), .clr(Clear));
  Register u_i1 (.D(Dip), .en(Cl), .clk(Cl), .Q(i1), .clr(Clear));
  Joystick joystick_1 (.x(joystick_1_x), .y(joystick_1_y));
  Register u_x0 (.D(O), .en(demultiplexer_1_out2), .clk(Cl), .Q(x0), .clr(Clear));
  Register u_x4 (.D(O), .en(demultiplexer_1_out6), .clk(Cl), .Q(x4), .clr(Clear));
  Register u_s1 (.D(O), .en(demultiplexer_1_out10), .clk(Cl), .Q(s1), .clr(Clear));
  Register u_i2 (.D({joystick_1_y, joystick_1_x}), .en(Cl), .clk(Cl), .Q(i2), .clr(Clear));
  Button button_1 (.out(button_3_out[2]));
  Button button_2 (.out(button_3_out[3]));
  Register u_x1 (.D(O), .en(demultiplexer_1_out3), .clk(Cl), .Q(x1), .clr(Clear));
  Register u_x5 (.D(O), .en(demultiplexer_1_out7), .clk(Cl), .Q(x5), .clr(Clear));
  Register u_s2 (.D(O), .en(demultiplexer_1_out11), .clk(Cl), .Q(s2), .clr(Clear));
  Register u_i3 (.D({button_3_out, button_7_out}), .en(Cl), .clk(Cl), .Q(i3), .clr(Clear));
  Button button_3 (.out(button_3_out[0]));
  Button button_4 (.out(button_7_out[2]));
  Button button_5 (.out(button_7_out[3]));
  Button button_6 (.out(button_3_out[1]));
  Button button_7 (.out(button_7_out[0]));
  Button button_8 (.out(button_7_out[1]));
  RAM #(.databus("bibus")) ram_1 (.addr(Operand), .we(WriteAdr), .oe(Cl), .clk(Cl), .din(O), .dout(RAMOut));
  TTY tty_1 (.data(s1[6:0]), .clk(Cl), .we(Cl));  // open: clr
  Keyboard keyboard_1 (.clk(Cl), .re(Cl), .avail(KB[7]), .data(KB[6:0]));  // open: clr
  ALU alu_1 (.Operation(Operation), .Operand(Operand), .A(A), .B(B), .O(ALUOut), .J(J));
  Multiplexer #(.select(4), .width(8), .enable("false")) multiplexer_1 (
    .in0({8{1'b0}}), .in1(ALUOut), .in2(ALUOut), .in3(ALUOut), .in4(ALUOut), .in5(ALUOut), .in6(ALUOut),
    .in7(ALUOut), .in8(ALUOut), .in9(Operand), .in10(RAMOut), .in11(RegisterRead), .in12({8{1'b0}}),
    .in13({8{1'b0}}), .in14({8{1'b0}}), .in15({8{1'b0}}), .out(O), .sel(Operation));
  DipSwitch dipswitch_1 (
    .sw1(Dip[7]), .sw2(Dip[6]), .sw3(Dip[5]), .sw4(Dip[4]), .sw5(Dip[3]), .sw6(Dip[2]), .sw7(Dip[1]),
    .sw8(Dip[0]));
  Multiplexer #(.select(4), .width(8), .enable("false")) multiplexer_2 (
    .in0(A), .in1(B), .in2(x0), .in3(x1), .in4(x2), .in5(x3), .in6(x4), .in7(x5), .in8(x6), .in9(s0),
    .in10(s1), .in11(s2), .in12(i0), .in13(i1), .in14(i2), .in15(i3), .out(RegisterRead), .sel(rs));
  Hex_Digit_Display hex_digit_display_1 (.value(s0[7:4]));  // open: dp
  // Probe on s0
  // BCD_to_7_Segment_decoder bcd_to_7_segment_decoder_1: pin names not known
  // _7_Segment_Display 7_segment_display_1: pin names not known; wires that end beside it: n7_segment_display_1_p1, n7_segment_display_1_p1
  Hex_Digit_Display hex_digit_display_2 (.value(s0[3:0]));  // open: dp
  // BCD_to_7_Segment_decoder bcd_to_7_segment_decoder_2: pin names not known
  // _7_Segment_Display 7_segment_display_2: pin names not known; wires that end beside it: n7_segment_display_2_p1, n7_segment_display_2_p1
  // Binairy_to_BCD_converter #(.binvalue(8)) binairy_to_bcd_converter_1: pin names not known; wires that end beside it: s0
  Demultiplexer #(.select(4), .enable("false")) demultiplexer_2 (
    .out1(demultiplexer_2_out1), .out2(demultiplexer_2_out2), .out3(demultiplexer_2_out3),
    .out4(demultiplexer_2_out4), .out5(demultiplexer_2_out5), .out6(demultiplexer_2_out6),
    .out7(demultiplexer_2_out7), .out8(demultiplexer_2_out8), .out9(demultiplexer_2_out9),
    .out10(demultiplexer_2_out10), .out11(WriteAdr), .in(1'b1), .sel(Operation));  // open: out0, out12, out13, out14, out15
  // BCD_to_7_Segment_decoder bcd_to_7_segment_decoder_3: pin names not known
  // _7_Segment_Display 7_segment_display_3: pin names not known; wires that end beside it: n7_segment_display_3_p1, n7_segment_display_3_p1
  or or_1 (RegEnable, demultiplexer_2_out1, demultiplexer_2_out2, demultiplexer_2_out3, demultiplexer_2_out4, demultiplexer_2_out5, demultiplexer_2_out6, demultiplexer_2_out7, demultiplexer_2_out8, demultiplexer_2_out9, demultiplexer_2_out10);

  // Notes on the sheet:
  //   contents of rom_1 (hex, n*v repeats v):
  //   9001 1100 b100 a900 d000 c000
  //   Hex Display
  //   BCD -> 7 Segment
endmodule

module FullAdder (
  input  A,
  input  B,
  input  Cin,
  output Cout,
  output S
);

  wire and_1_out, and_2_out, xor_1_out;

  xor xor_1 (xor_1_out, A, B);
  and and_1 (and_1_out, A, B);
  and and_2 (and_2_out, Cin, xor_1_out);
  xor xor_2 (S, xor_1_out, Cin);
  or or_1 (Cout, and_2_out, and_1_out);
endmodule

module EightBitAdder (
  input  [7:0] A,
  input  [7:0] B,
  input  C,
  output [7:0] O
);

  wire fulladder_1_cout, fulladder_2_cout, fulladder_3_cout, fulladder_4_cout, fulladder_5_cout,
       fulladder_7_cout, fulladder_8_cout;

  FullAdder fulladder_1 (.A(A[0]), .B(B[0]), .Cin(C), .Cout(fulladder_1_cout), .S(O[0]));
  FullAdder fulladder_2 (.A(A[3]), .B(B[3]), .Cin(fulladder_7_cout), .Cout(fulladder_2_cout), .S(O[3]));
  FullAdder fulladder_3 (.A(A[6]), .B(B[6]), .Cin(fulladder_8_cout), .Cout(fulladder_3_cout), .S(O[6]));
  FullAdder fulladder_4 (.A(A[1]), .B(B[1]), .Cin(fulladder_1_cout), .Cout(fulladder_4_cout), .S(O[1]));
  FullAdder fulladder_5 (.A(A[4]), .B(B[4]), .Cin(fulladder_2_cout), .Cout(fulladder_5_cout), .S(O[4]));
  FullAdder fulladder_6 (.A(A[7]), .B(B[7]), .Cin(fulladder_3_cout), .S(O[7]));  // open: Cout
  FullAdder fulladder_7 (.A(A[2]), .B(B[2]), .Cin(fulladder_4_cout), .Cout(fulladder_7_cout), .S(O[2]));
  FullAdder fulladder_8 (.A(A[5]), .B(B[5]), .Cin(fulladder_5_cout), .Cout(fulladder_8_cout), .S(O[5]));
endmodule

module ALU (
  input  [3:0] Operation,
  input  [7:0] Operand,
  input  [7:0] A,
  input  [7:0] B,
  output [7:0] O,
  output J
);

  wire comparator_1_eq, comparator_1_gt, comparator_1_lt, not_3_out;
  wire [7:0] Add_o, and_1_out, not_1_out, not_2_out, or_1_out, shifter_1_out, shifter_2_out, Sub_o, xor_1_out;

  assign not_1_out = ~B;  // NOT_Gate not_1, 8 bits wide
  EightBitAdder Add (.A(A), .B(B), .C(1'b0), .O(Add_o));
  EightBitAdder Sub (.A(A), .B(not_1_out), .C(1'b1), .O(Sub_o));
  assign and_1_out = A & B;  // AND_Gate and_1, 8 bits wide
  assign not_2_out = ~A;  // NOT_Gate not_2, 8 bits wide
  assign or_1_out = A | B;  // OR_Gate or_1, 8 bits wide
  assign xor_1_out = A ^ B;  // XOR_Gate xor_1, 8 bits wide
  Shifter shifter_1 (.in(A), .\dist (Operand[2:0]), .out(shifter_1_out));
  Shifter #(.shift("lr")) shifter_2 (.in(A), .\dist (Operand[2:0]), .out(shifter_2_out));
  Comparator #(.mode("unsigned")) comparator_1 (
    .a(A), .b(B), .gt(comparator_1_gt), .eq(comparator_1_eq), .lt(comparator_1_lt));
  not not_3 (not_3_out, comparator_1_eq);
  Multiplexer #(.select(4), .width(8), .enable("false")) multiplexer_1 (
    .in0({8{1'b0}}), .in1(Add_o), .in2(Sub_o), .in3(and_1_out), .in4(not_2_out), .in5(or_1_out),
    .in6(xor_1_out), .in7(shifter_1_out), .in8(shifter_2_out), .in9({8{1'b0}}), .in10({8{1'b0}}),
    .in11({8{1'b0}}), .in12({8{1'b0}}), .in13({8{1'b0}}), .in14({8{1'b0}}), .in15({8{1'b0}}), .out(O),
    .sel(Operation));
  Multiplexer #(.select(4), .enable("false")) multiplexer_2 (
    .in0(1'b0), .in1(1'b0), .in2(1'b0), .in3(1'b0), .in4(1'b0), .in5(1'b0), .in6(1'b0), .in7(1'b0),
    .in8(1'b0), .in9(1'b0), .in10(1'b0), .in11(1'b0), .in12(comparator_1_eq), .in13(not_3_out),
    .in14(comparator_1_gt), .in15(comparator_1_lt), .out(J), .sel(Operation));
endmodule
